# Fritzing sketch Arduino_Uno_NivelFoso_Breadboard (saved by Fritzing 0.9.3b)

parts:
  Part1 = Arduino Uno (Rev3) - ICSP
  hc-sr1 = hc-sr04
  KY-1 = Keyes Relay [package=THT]

nets:
  N1: Part1.D8, KY-1.power
  N2: Part1.D6_PWM, hc-sr1.Echo
  N3: Part1.D7, hc-sr1.Trig
  5V: Part1.5V, hc-sr1.VCC
  GND: Part1.GND, hc-sr1.GND

custom parts:
  Keyes Relay: The Keyes 5V relay module is suitable for SCM development, home appliance control. It uses a 5V~12V TIL control signal which can control DC / AC signal.
